# Fritzing sketch sensor_wiring (saved by Fritzing 0.7.5b)
breadboards: 1

parts:
  Part1 = Humidity Sensor - HIH-4030 Breakout
  R1 = Photocell (LDR) [package=THT]
  Part2 = Digital Temperature Sensor Breakout - TMP102
  Arduino1 = Arduino  # not connected
  R2 = Resistor [tolerance=±5% resistance=100k package=THT]
  Part5 = Arduino WiFly Shield

nets:
  GND: Part1.GND, Part2.GND, Part2.ADD0, R2.Pin_1, Part5.GND
  N1: Part1.OUT, Part5.A1
  VCC: Part1.VCC, R1.pin_0, Part5.5V
  N2: R1.pin_1, R2.Pin_0, Part5.A0
  N3: Part2.V+, Part5.3.3
  N4: Part2.SDA, Part5.A4
  N5: Part2.SCL, Part5.A5
